// Logisim project logickaKola.circ as structural Verilog: 6 circuits, main circuit main
module main (
  input  in_1,
  input  in_2,
  input  in_3,
  input  in_4,
  input  in_5,
  input  in_6,
  input  in_7,
  input  in_8,
  input  in_9,
  input  in_10,
  input  in_11,
  output out_12,
  output out_13,
  output out_14,
  output out_15,
  output out_16,
  output out_17
);

  and AND (out_12, in_1, in_3);
  xor XOR (out_14, in_5, in_7);
  nand NAND (out_16, in_8, in_10);
  or OR (out_13, in_2, in_4);
  not NOT (out_15, in_6);
  nor NOR (out_17, in_9, in_11);
endmodule

module primerMini (
  input  A,
  input  B,
  output out_3,
  output out_4
);

  wire and_1_out, and_2_out, not_1_out;

  and and_1 (and_1_out, A, B);
  not not_1 (not_1_out, B);
  and and_2 (and_2_out, not_1_out, A);
  or or_1 (out_3, and_1_out, and_2_out);

  assign out_4 = A;
endmodule

module primerMUX (
  input  in_1,
  input  in_2,
  input  in_3,
  input  in_4,
  input  in_5,
  input  in_6,
  output out_7,
  output out_8
);

  wire and_1_out, and_2_out, not_1_out;

  not not_1 (not_1_out, in_1);
  Multiplexer multiplexer_1 (.in0(in_5), .in1(in_6), .out(out_8), .sel(in_4));  // open: en
  and and_1 (and_1_out, not_1_out, in_2);
  and and_2 (and_2_out, in_1, in_3);
  or or_1 (out_7, and_1_out, and_2_out);
endmodule

module primerSabirac (
  input  A,
  input  B,
  input  A_2,
  input  B_2,
  output C,
  output C_2,
  output P,
  output P_2
);

  wire and_1_out, and_2_out, not_1_out, not_2_out;

  not not_1 (not_1_out, A);
  not not_2 (not_2_out, B);
  and and_1 (and_1_out, not_1_out, B);
  and and_2 (and_2_out, not_2_out, A);
  and and_3 (P_2, B, A);
  or or_1 (C_2, and_1_out, and_2_out);
  xor xor_1 (C, B_2, A_2);
  and and_4 (P, A_2, B_2);
endmodule

module _0_2_5_3_0 (
);

  wire and_1_out, B_q, C_qn, clock_1_out;

  Clock clock_1 (.out(clock_1_out));
  J_K_Flip_Flop A (.J(and_1_out), .clk(clock_1_out), .K(1'b1));  // open: Q, Qn, preset, en, reset
  and and_1 (and_1_out, C_qn, B_q);
  J_K_Flip_Flop B (.J(1'b1), .clk(clock_1_out), .K(1'b1), .Q(B_q));  // open: Qn, preset, en, reset
  J_K_Flip_Flop C (.J(B_q), .clk(clock_1_out), .K(B_q), .Qn(C_qn));  // open: Q, preset, en, reset
endmodule

module simpleALU (
  input  [3:0] in_1,
  input  [1:0] in_2,
  output [3:0] out_3
);

  wire [3:0] adder_1_out, not_4_out;

  not not_1 (not_4_out[1], in_1[1]);
  not not_2 (not_4_out[2], in_1[2]);
  not not_3 (not_4_out[3], in_1[3]);
  not not_4 (not_4_out[0], in_1[0]);
  Adder #(.width(4)) adder_1 (.a(4'b0001), .b(in_1), .out(adder_1_out));  // open: cin, cout
  Multiplexer #(.select(2), .width(4)) multiplexer_1 (
    .in0(not_4_out), .in1(adder_1_out), .in2({in_1[2:0], in_1[0]}), .in3(in_1), .out(out_3), .sel(in_2));  // open: en
endmodule
